# Fritzing sketch PowerIndicator.01 (saved by Fritzing 0.9.2b)
circuit board: 3.64299cm x 2.41026cm
breadboards: 1

parts:
  U1 = LM 358 Dual Op-Amp [part_number="LM358 or TS393CN" package="DIP8 [THT]"]
  R1 = Resistor [tolerance=±5% resistance=25k package=THT]
  R2 = Resistor [tolerance=±5% resistance=1.5M package=THT]
  R3 = Resistor [tolerance=±5% resistance=50k package=THT]
  R4 = Resistor [tolerance=±5% resistance=39k package=THT]
  R5 = Resistor [tolerance=±5% resistance=1k package=THT]
  R6 = Resistor [tolerance=±5% resistance=1k package=THT]
  8x_AA_or_3x_18605 = DC Power [voltage=12V]
  U2 = V_REG_LD1117VXX [package=78xxl]
  LED2 = DUO LED RG [part_number=SSL-LX3059IGW-CA package="5 mm [THT]"]

nets:
  N1: U1.connector0, U1.connector5, R2.Pin_1, R5.Pin_0
  N2: U1.connector1, R3.Pin_0, R4.Pin_1
  N3: U1.connector2, R1.Pin_1, R2.Pin_0
  GND: U1.connector3, R4.Pin_0, 8x_AA_or_3x_18605.V-, U2.GND
  N4: U1.connector4, R1.Pin_0, U2.OUT, LED2.common_cathode
  N5: U1.connector6, R6.Pin_0
  N6: U1.connector7, R3.Pin_1, 8x_AA_or_3x_18605.V+, U2.IN
  N7: R5.Pin_1, LED2.green_anode
  N8: R6.Pin_1, LED2.red_anode

notes:
  Power Indicator, Power on and low battery indicator.  Glows green if battery voltage >8.9V.   Glows red otherwise., 0.2
