# Fritzing sketch PowerIndicatorBlinker.01 (saved by Fritzing 0.9.2b)
breadboards: 1

parts:
  U1 = LM 358 Dual Op-Amp [part_number=LM358 package="DIP8 [THT]"]
  R1 = Resistor [tolerance=±5% resistance=25k package=THT]
  R2 = Resistor [tolerance=±5% resistance=1M package=THT]
  R3 = Resistor [tolerance=±5% resistance=50k package=THT]
  R4 = Resistor [tolerance=±5% resistance=39k package=THT]
  R5 = Resistor [tolerance=±5% resistance=1k package=THT]
  R6 = Resistor [tolerance=±5% resistance=1k package=THT]
  C1 = Ceramic Capacitor [capacitance=0.1µF voltage=16V package="200 mil [THT, multilayer]"]
  R7 = Resistor [tolerance=±5% resistance=100k package=THT]
  R8 = Resistor [tolerance=±5% resistance=10M package=THT]
  R9 = Resistor [tolerance=±5% resistance=100k package=THT]
  D1 = Diode [part_number=1N4148 package=diode-1n4001]
  8x_AA_or_3x_18606 = DC Power [voltage=12V]
  U2 = V_REG_LD1117VXX [package=78xxl]
  LED1 = DUO LED RG [package="5 mm [THT]"]

nets:
  N1: U1.connector0, R2.Pin_1, R5.Pin_0, R7.Pin_1
  N2: U1.connector1, R3.Pin_0, R4.Pin_1
  N3: U1.connector2, R1.Pin_1, R2.Pin_0
  GND: U1.connector3, R4.Pin_0, C1.0, 8x_AA_or_3x_18606.V-, U2.GND
  N4: U1.connector4, R1.Pin_0, U2.OUT, LED1.common_cathode
  N5: U1.connector5, C1.1, R7.Pin_0, R8.Pin_0, R9.Pin_0
  N6: U1.connector6, R6.Pin_0, R8.Pin_1, D1.C
  N7: U1.connector7, R3.Pin_1, 8x_AA_or_3x_18606.V+, U2.IN
  N8: R5.Pin_1, LED1.green_anode
  N9: R6.Pin_1, LED1.red_anode
  N10: R9.Pin_1, D1.A

notes:
  Power Indicator, Power on and low battery indicator.  Glows green if battery voltage >8.9V.   Blinks red otherwise., 0.2
